# Fritzing sketch main (saved by Fritzing 0.9.10b)
breadboards: 3

parts:
  ZS-042_RTC1 = ZS-042 RTC Module  # not connected
  Q1 = MOSFET-NCHANNEL [package=to220v]
  元件1 = Arduino Nano (Rev3.0)
  元件4 = Bluetooth HC-05 Macho  # not connected
  M1 = RioRand LM2596
  元件19 = InvenSense MPU6050
  Serial_Port_Connector1 = Serial Port Connector  # not connected
  元件47 = Adafruit Ultimate GPS v3 [part_number="Adafruit #746"]
  元件48 = INA219 High Side DC Current Sensor Breakout [part_number=904]
  元件49 = Lithium Ion Cylindrical Battery 3.7v 2200mAh [part_number=1781]
  D1 = SOLAR-IXYS [package=solarbit-12x1]  # not connected
  U10 = LCD-16X2 [package=lcd-16x2_noholes]  # not connected
  元件41 = Adafruit TCA9548A
  元件5 = PowerBoost 500 Charger  # not connected
  D2 = Schottky Diode [part_number=1N5817 package="Melf DO-213 AB [SMD]"]
  D3 = Schottky Diode [part_number=1N5817 package="Melf DO-213 AB [SMD]"]

nets:
  N1: Q1.D, D3.anode
  N2: Q1.S, D2.cathode
  GND: 元件1.GND, M1.Pin_4, 元件19.GND, 元件47.GND, 元件41.GND
  N3: 元件1.VIN, D3.cathode
  5V: 元件1.5V, 元件41.VCC
  N4: 元件1.A5, 元件41.INPUTSCL
  N5: 元件1.A4, 元件41.INPUTSDA
  3V3: 元件1.3V3, 元件19.VCC, 元件47.3.3V
  N6: M1.Pin_1, 元件49.positive
  N7: M1.Pin_2, 元件49.negative
  N8: M1.Pin_3, D2.anode
  N9: 元件19.SDA, 元件41.1SCL
  N10: 元件19.XDA, 元件41.1SDA
  N11: 元件48.VIN-, 元件48.SCL, 元件48.SDA, 元件48.VIN+

notes:
  nano：
  紅線：6v直接出來
  橘線：5v
  粉線：3.3v
  GPS：3.3v
  gy91：3.3v
  RTC：2.3-5.5，可低電壓
  衛星：3.5-5.4v，推薦5v
  H05：工作3.6-6，5v
  MUX：工作1.65-5.5v
  推薦5v
  電源監測：工作3-5.5v，感測0-26v

custom parts:
  Adafruit Ultimate GPS v3: We carry a few different GPS modules here in the Adafruit shop, but none that satisfied our every desire - that's why we designed this little GPS breakout board. We believe this is the Ultimate GPS module, so we named it that. It's got everything you want and more: -165 dBm sensitivity, 10 Hz updates, 66 channels 5V friendly design and only 20mA current draw Breadboard friendly + two mounting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
  INA219 High Side DC Current Sensor Breakout: This breakout board will solve all your power-monitoring problems. Instead of struggling with two multimeters, you can just use the handy INA219B chip on this breakout to both measure both the high side voltage and DC current draw over I2C with 1% precision. Most current-measuring devices such as our current panel meter are only good for low side measuring. That means that unless you want to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
  Lithium Ion Cylindrical Battery 3.7v 2200mAh: This lithium ion battery has a capacity of 2200mAh and a protection circuit that provides over-voltage, under-voltage and over-current protection. This cell can provide 2C of peak current (4400mA). Note that these batteries are not designed to sustain such high loads, we suggest keeping any constant current draw under about 0.5C (1 Amp).
  Adafruit TCA9548A: You just found the perfect I2C sensor, and you want to wire up two or three or more of them to your Arduino when you realize "Uh oh, this chip has a fixed I2C address, and from what I know about I2C, you cannot have two devices with the same address on the same SDA/SCL pins!" Are you out of luck? You would be, if you didn't have this ultra-cool TCA9548A 1-to-8 I2C multiplexer! Finally, a way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
